// Digital circuit CPU8Bit1K.dig as structural Verilog
module CPU8Bit1K (
  input  in_1,
  input  in_2,
  input  [7:0] IN,
  output CLK,
  output LDROM,
  output IRZ,
  output MUX,
  output OP0,
  output OP1,
  output OP2,
  output OP3,
  output BE,
  output BOE,
  output ARE,
  output RAME,
  output RAMOE,
  output [7:0] A,
  output [7:0] B,
  output [9:0] AR,
  output AE,
  output [9:0] PC,
  output [7:0] IR,
  output [7:0] BUS,
  output E,
  output G,
  output S,
  output N,
  output C,
  output Z,
  output PCM0,
  output PCM1,
  output PCM2,
  output RAMAMUX,
  output PROMAMUX,
  output [7:0] PROM,
  output [1:0] A89,
  output [7:0] OUT
);

  wire AINC, ARINC, AROE, BINC, CARRY_q, CCLR, CE, CSET, INE, multiplexer_1_out, or_1_out, OUTE, XXX;
  wire [7:0] alu8bits_1_y, Demux_o0;
  wire [7:6] alu8bits_1_st;
  wire [9:0] multiplexer_2_out, multiplexer_3_out;

  Multiplexer #(.Selector_Bits(3)) multiplexer_1 (
    .sel({PCM2, PCM1, PCM0}), .in_0(1'b0), .in_1(1'b1), .in_2(Z), .in_3(E), .in_4(G), .in_5(S), .in_6(N),
    .in_7(C), .out(multiplexer_1_out));
  or or_1 (or_1_out, CCLR, in_2);
  Reg8i u_A (.E(AE), .INC(AINC), .CLK(in_1), .R(in_2), .D(Demux_o0), .Q(A));
  BasicReg1 CARRY (.Q(CARRY_q), .S(CSET), .D(C), .E(CE), .CLK(in_1), .R(or_1_out));
  Reg10ir u_PC (.E(multiplexer_1_out), .INC(1'b1), .nCLK(in_1), .R(in_2), .D({A89, PROM}), .Q(PC));
  BasicReg8 u_In (.Q(BUS), .D(IN), .E(INE), .CLK(in_1), .R(in_2));
  ALU8Bits alu8bits_1 (
    .Y(alu8bits_1_y), .A(A), .B(BUS), .ST({alu8bits_1_st, C, N, S, G, E, Z}), .Cin(CARRY_q),
    .OP({OP3, OP2, OP1, OP0}));
  Multiplexer #(.Bits(10)) multiplexer_2 (.sel(PROMAMUX), .in_0(PC), .in_1(AR), .out(multiplexer_2_out));
  ROM #(.AddrBits(10), .Bits(8)) u_PROM (.A(multiplexer_2_out), .sel(1'b1), .D(PROM));
  Demux8 Demux (.O0(Demux_o0), .O1(BUS), .I(alu8bits_1_y), .S(MUX));
  Reg8i u_B (.E(BE), .INC(BINC), .CLK(in_1), .R(in_2), .D(BUS), .Q(B));
  BasicReg8 u_Out (.Q(OUT), .D(BUS), .E(OUTE), .CLK(in_1), .R(in_2));
  assign BUS = BOE ? B : 8'bz;  // Driver driver_1
  assign BUS = LDROM ? PROM : 8'bz;  // Driver driver_2
  Reg10i u_AR (.E(ARE), .INC(ARINC), .CLK(in_1), .R(in_2), .D({A89, BUS}), .Q(AR));
  Multiplexer #(.Bits(10)) multiplexer_3 (.sel(RAMAMUX), .in_0(AR), .in_1({A89, PROM}), .out(multiplexer_3_out));
  RAMSinglePort #(.AddrBits(10), .Bits(8)) RAM (.A(multiplexer_3_out), .str(RAME), .C(in_1), .ld(RAMOE), .D(BUS));
  Reg8 u_IR (.D(PROM), .Q({A89, IR[5:0]}), .SR(IRZ), .nCLK(in_1), .R(in_2));
  ROM #(.AddrBits(6), .Bits(28)) rom_1 (
    .A(IR[5:0]), .sel(1'b1),
    .D({XXX, CE, CCLR, CSET, INE, OUTE, AROE, ARINC, BINC, AINC, PROMAMUX, RAMAMUX, PCM2, PCM1, PCM0, RAMOE, RAME, ARE, BOE, BE, OP3, OP2, OP1, OP0, MUX, IRZ, AE, LDROM}));

  assign CLK = in_1;
  assign IR[7:6] = A89;

  // Other names for the same wires on the sheet: RESET = in_2

  // Notes on the sheet:
  //   in_2: default 1
  //   contents of PROM (hex, n*v repeats v):
  //   0,43,9,6*0,a,c,2,2,b,11
  //   contents of rom_1 (hex, n*v repeats v):
  //   0,17,105,405,108,212,408,412,808,a00,1080c,10a04,2004,4004
endmodule
